# Fritzing sketch hardware (saved by Fritzing 0.9.2b)

parts:
  IR1 = TSOP312.., 314.. [package=THT]
  LED1 = LEDs [package=led10mm]
  Part1 = Arduino Uno (Rev3)
  LED2 = LED - 5mm [color="Red (633nm)" package="5 mm [THT]"]
  R1 = Resistor [tolerance=±5% resistance=220 package=THT]  # not connected

nets:
  N1: IR1.Vs, LED1.A, Part1.GND, LED2.cathode
  N2: IR1.Data, Part1.VIN
  N3: LED1.C, Part1.D3_PWM
  N4: Part1.D13/SCK, LED2.anode
